// Logisim project 27-10-2022.circ as structural Verilog: 1 circuit, main circuit main
module main (
  input  A,
  input  B,
  input  C,
  output X
);

  wire and_1_out, and_2_out, not_1_out, not_2_out, not_3_out, or_1_out, or_2_out;

  and and_1 (and_1_out, B, C);
  not not_1 (not_1_out, B);
  or or_1 (or_1_out, A, and_1_out);
  and and_2 (and_2_out, not_1_out, A);
  not not_2 (not_2_out, or_1_out);
  not not_3 (not_3_out, and_2_out);
  not not_4 (X, or_2_out);
  or or_2 (or_2_out, not_2_out, not_3_out);
endmodule
