// Logisim project BTTT.circ as structural Verilog: 6 circuits, main circuit main
module main (
  input  A,
  input  B,
  output S,
  output C
);

  xor xor_1 (S, A, B);
  and and_1 (C, A, B);
endmodule

module HA (
  input  A,
  input  B,
  output S,
  output C
);

  xor xor_1 (S, A, B);
  and and_1 (C, A, B);
endmodule

module FA (
  input  A,
  input  B,
  input  Cin,
  output S,
  output Cout
);

  wire and_1_out, ha_1_c, ha_1_s;

  HA ha_1 (.A(A), .B(B), .S(ha_1_s), .C(ha_1_c));
  and and_1 (and_1_out, ha_1_s, Cin);
  xor xor_1 (S, ha_1_s, Cin);
  xor xor_2 (Cout, ha_1_c, and_1_out);
endmodule

module C3 (
  input  A3,
  input  B3,
  input  CI3,
  input  A2,
  input  B2,
  input  A1,
  input  B1,
  input  A0,
  input  B0,
  output S3,
  output S2,
  output S1,
  output S0,
  output Cout
);

  wire fa_1_cout, fa_2_cout, fa_3_cout;

  FA fa_1 (.A(A3), .B(B3), .Cin(CI3), .S(S3), .Cout(fa_1_cout));
  FA fa_2 (.A(A2), .B(B2), .Cin(fa_1_cout), .S(S2), .Cout(fa_2_cout));
  FA fa_3 (.A(A1), .B(B1), .Cin(fa_2_cout), .S(S1), .Cout(fa_3_cout));
  FA fa_4 (.A(A0), .B(B0), .Cin(fa_3_cout), .S(S0), .Cout(Cout));
endmodule

module c4 (
  input  I3,
  input  I2,
  input  I1,
  input  I0,
  output A,
  output B,
  output C,
  output D,
  output E,
  output F,
  output G
);

  wire and_1_out, and_2_out, and_3_out, and_4_out, and_5_out, and_6_out, and_7_out, and_8_out, and_9_out,
       and_10_out, and_11_out, and_12_out, and_13_out, and_14_out, and_15_out, and_16_out, and_17_out,
       not_1_out, not_2_out, not_3_out, not_4_out;

  not not_1 (not_1_out, I3);
  not not_2 (not_2_out, I2);
  not not_3 (not_3_out, I1);
  not not_4 (not_4_out, I0);
  and and_1 (and_1_out, not_1_out, not_2_out, not_3_out, I0);
  and and_2 (and_2_out, I2, not_3_out, not_4_out);
  and and_3 (and_3_out, I3, I1);
  and and_4 (and_4_out, I2, not_3_out);
  and and_5 (and_5_out, I2, not_4_out);
  and and_6 (and_6_out, I3, I1);
  and and_7 (and_7_out, not_2_out, I1, not_4_out);
  and and_8 (and_8_out, I3, I1);
  and and_9 (and_9_out, not_1_out, not_2_out, not_3_out, I0);
  and and_10 (and_10_out, I2, I1, I0);
  and and_11 (and_11_out, I2, not_3_out);
  and and_12 (and_12_out, not_1_out, not_2_out, I0);
  and and_13 (and_13_out, not_2_out, I1);
  and and_14 (and_14_out, I2, not_3_out, not_4_out);
  and and_15 (and_15_out, I1, I0);
  and and_16 (and_16_out, not_1_out, not_2_out, not_3_out);
  and and_17 (and_17_out, I3, I1);
  or or_1 (A, and_1_out, and_2_out, and_3_out);
  or or_2 (B, and_4_out, and_5_out, and_6_out);
  or or_3 (C, and_7_out, and_8_out);
  or or_4 (D, and_9_out, and_10_out);
  or or_5 (E, I0, and_11_out);
  or or_6 (F, and_12_out, and_13_out, and_14_out, and_15_out);
  or or_7 (G, and_16_out, and_17_out);
endmodule

module C4_LED7DOAN (
  input  I3,
  input  I2,
  input  I1,
  input  I0
);

  wire c4_1_a, c4_1_b, c4_1_c, c4_1_d, c4_1_e, c4_1_f, c4_1_g;

  c4 c4_1 (
    .I3(I3), .I2(I2), .I1(I1), .I0(I0), .A(c4_1_a), .B(c4_1_b), .C(c4_1_c), .D(c4_1_d), .E(c4_1_e),
    .F(c4_1_f), .G(c4_1_g));
  _7_Segment_Display #(.active("false")) u_7_segment_display_1 (
    .g(c4_1_g), .f(c4_1_f), .a(c4_1_a), .b(c4_1_b), .e(c4_1_e), .d(c4_1_d), .c(c4_1_c));  // open: dp
endmodule
