// Logisim project LAB04.circ as structural Verilog
module Mss (
  input  G,
  input  A,
  input  B,
  output S,
  output E,
  output I
);

  wire not_1_out, not_2_out, not_3_out, or_1_out;

  not not_1 (not_1_out, A);
  not not_2 (not_2_out, B);
  and and_1 (S, A, not_2_out, G);
  and and_2 (I, not_1_out, B, G);
  or or_1 (or_1_out, S, I);
  not not_3 (not_3_out, or_1_out);
  and and_3 (E, not_3_out, G);
endmodule

module BT (
  input  A1,
  input  B1,
  input  A2,
  input  B2,
  input  A3,
  input  B3,
  input  A4,
  input  B4,
  output S,
  output I,
  output E
);

  wire mss_1_e, mss_1_i, mss_1_s, mss_2_e, mss_2_i, mss_2_s, mss_3_e, mss_3_i, mss_3_s, mss_4_i, mss_4_s;

  Mss mss_1 (.G(1'b1), .A(A1), .B(B1), .S(mss_1_s), .E(mss_1_e), .I(mss_1_i));
  Mss mss_2 (.G(mss_1_e), .A(A2), .B(B2), .S(mss_2_s), .E(mss_2_e), .I(mss_2_i));
  Mss mss_3 (.G(mss_2_e), .A(A3), .B(B3), .S(mss_3_s), .E(mss_3_e), .I(mss_3_i));
  Mss mss_4 (.G(mss_3_e), .A(A4), .B(B4), .S(mss_4_s), .E(E), .I(mss_4_i));
  or or_1 (S, mss_1_s, mss_2_s, mss_3_s, mss_4_s);
  or or_2 (I, mss_1_i, mss_2_i, mss_3_i, mss_4_i);
endmodule

module Bai (
  input  E,
  input  A,
  input  B,
  input  C,
  input  D,
  output a1,
  output b1,
  output c1,
  output d1,
  output e1,
  output f1,
  output g1,
  output a2,
  output b2,
  output c2,
  output d2,
  output e2,
  output f2,
  output g2
);

  wire and_1_out, and_2_out, and_3_out, and_4_out, and_5_out, and_6_out, and_7_out, and_8_out, and_9_out,
       and_10_out, and_11_out, and_12_out, and_13_out, and_14_out, and_15_out, and_16_out, and_17_out,
       and_18_out, and_19_out, and_20_out, and_21_out, and_22_out, and_23_out, and_24_out, and_25_out,
       and_26_out, and_27_out, and_28_out, and_29_out, and_30_out, and_31_out, and_32_out, and_33_out,
       and_34_out, and_35_out, and_36_out, and_37_out, and_38_out, and_39_out, and_40_out, and_41_out,
       and_42_out, and_43_out, and_44_out, and_45_out, and_46_out, and_47_out, and_48_out, and_49_out,
       and_50_out, and_51_out, and_52_out, and_53_out, and_54_out, and_55_out, and_56_out, and_57_out,
       and_58_out, and_59_out, and_60_out, and_61_out, and_62_out, and_63_out, and_64_out, and_65_out,
       and_66_out, and_67_out, and_68_out, and_69_out, and_70_out, and_71_out, and_72_out, and_73_out,
       and_74_out, and_75_out, and_76_out, and_77_out, and_78_out, and_79_out, and_80_out, and_81_out,
       and_82_out, and_83_out, and_84_out, and_85_out, and_86_out, and_87_out, and_88_out, and_89_out,
       not_1_out, not_2_out, not_3_out, not_4_out, not_5_out;

  not not_1 (not_1_out, E);
  not not_2 (not_2_out, A);
  not not_3 (not_3_out, B);
  not not_4 (not_4_out, C);
  not not_5 (not_5_out, D);
  and and_1 (and_1_out, not_1_out, not_2_out);
  and and_2 (and_2_out, E, A);
  and and_3 (and_3_out, not_1_out, not_3_out, not_4_out);
  and and_4 (and_4_out, not_2_out, B);
  and and_5 (and_5_out, not_2_out, not_3_out);
  and and_6 (and_6_out, A, B, C);
  and and_7 (and_7_out, not_1_out, not_2_out);
  and and_8 (and_8_out, E, A);
  and and_9 (and_9_out, not_1_out, not_3_out, not_4_out);
  and and_10 (and_10_out, not_2_out, B);
  and and_11 (and_11_out, not_1_out, not_2_out);
  and and_12 (and_12_out, not_2_out, B);
  and and_13 (and_13_out, E, A, not_3_out);
  and and_14 (and_14_out, not_1_out, not_3_out, not_4_out);
  and and_15 (and_15_out, E, B, not_4_out);
  and and_16 (and_16_out, not_1_out, not_2_out);
  and and_17 (and_17_out, not_1_out, not_3_out, not_4_out);
  and and_18 (and_18_out, E, B);
  and and_19 (and_19_out, E, A);
  and and_20 (and_20_out, not_2_out, C);
  and and_21 (and_21_out, not_1_out, B, D);
  and and_22 (and_22_out, not_1_out, not_3_out, not_5_out);
  and and_23 (and_23_out, not_1_out, A, not_4_out);
  and and_24 (and_24_out, not_2_out, not_3_out, not_5_out);
  and and_25 (and_25_out, E, not_2_out, not_3_out);
  and and_26 (and_26_out, E, not_2_out, not_5_out);
  and and_27 (and_27_out, E, not_3_out, D);
  and and_28 (and_28_out, not_3_out, C, not_5_out);
  and and_29 (and_29_out, A, B, not_4_out);
  and and_30 (and_30_out, E, B, not_5_out);
  and and_31 (and_31_out, not_2_out, C, D);
  and and_32 (and_32_out, A, not_4_out, not_5_out);
  and and_33 (and_33_out, not_1_out, not_3_out);
  and and_34 (and_34_out, not_1_out, not_4_out, not_5_out);
  and and_35 (and_35_out, not_1_out, A, not_4_out);
  and and_36 (and_36_out, not_1_out, A, not_5_out);
  and and_37 (and_37_out, not_2_out, not_3_out, D);
  and and_38 (and_38_out, not_2_out, not_3_out, C);
  and and_39 (and_39_out, B, not_4_out, not_5_out);
  and and_40 (and_40_out, E, not_2_out, D);
  and and_41 (and_41_out, E, not_2_out, C);
  and and_42 (and_42_out, not_3_out, C, D);
  and and_43 (and_43_out, A, B, not_4_out);
  and and_44 (and_44_out, A, B, not_5_out);
  and and_45 (and_45_out, E, C, D);
  and and_46 (and_46_out, E, not_3_out);
  and and_47 (and_47_out, not_2_out, not_4_out);
  and and_48 (and_48_out, not_1_out, not_2_out, B);
  and and_49 (and_49_out, not_3_out, not_4_out);
  and and_50 (and_50_out, A, not_3_out);
  and and_51 (and_51_out, not_1_out, B, C);
  and and_52 (and_52_out, E, not_4_out);
  and and_53 (and_53_out, A, C);
  and and_54 (and_54_out, not_2_out, not_3_out, C);
  and and_55 (and_55_out, not_1_out, B, not_4_out, D);
  and and_56 (and_56_out, not_2_out, C, not_5_out);
  and and_57 (and_57_out, not_1_out, A, B, D);
  and and_58 (and_58_out, E, not_2_out, C);
  and and_59 (and_59_out, A, not_4_out, D);
  and and_60 (and_60_out, not_1_out, not_3_out, not_5_out);
  and and_61 (and_61_out, not_1_out, A, not_4_out);
  and and_62 (and_62_out, not_2_out, not_3_out, not_5_out);
  and and_63 (and_63_out, E, not_2_out, not_5_out);
  and and_64 (and_64_out, not_3_out, C, not_5_out);
  and and_65 (and_65_out, A, B, not_4_out);
  and and_66 (and_66_out, E, C, not_5_out);
  and and_67 (and_67_out, not_2_out, C, not_5_out);
  and and_68 (and_68_out, not_2_out, not_3_out, not_5_out);
  and and_69 (and_69_out, not_1_out, not_3_out, not_5_out);
  and and_70 (and_70_out, not_1_out, A, not_4_out, not_5_out);
  and and_71 (and_71_out, E, not_2_out, not_5_out);
  and and_72 (and_72_out, not_3_out, C, not_5_out);
  and and_73 (and_73_out, A, B, not_4_out, not_5_out);
  and and_74 (and_74_out, E, C, not_5_out);
  and and_75 (and_75_out, not_1_out, not_2_out, B, not_4_out);
  and and_76 (and_76_out, A, not_3_out, not_4_out);
  and and_77 (and_77_out, not_1_out, A, B, C);
  and and_78 (and_78_out, E, not_2_out, not_3_out, C);
  and and_79 (and_79_out, E, A, not_4_out);
  and and_80 (and_80_out, not_2_out, not_4_out, not_5_out);
  and and_81 (and_81_out, A, C, not_5_out);
  and and_82 (and_82_out, not_1_out, not_2_out, B, not_5_out);
  and and_83 (and_83_out, not_2_out, not_3_out, C);
  and and_84 (and_84_out, not_1_out, B, not_4_out);
  and and_85 (and_85_out, A, not_4_out);
  and and_86 (and_86_out, E, not_3_out, not_5_out);
  and and_87 (and_87_out, not_1_out, A, B);
  and and_88 (and_88_out, E, not_2_out, C);
  and and_89 (and_89_out, not_2_out, C, not_5_out);
  or or_1 (a1, and_1_out, and_2_out, and_3_out, and_4_out);
  or or_2 (c1, not_1_out, and_5_out, and_6_out);
  or or_3 (d1, and_7_out, and_8_out, and_9_out, and_10_out);
  or or_4 (e1, and_11_out, and_12_out, and_13_out, and_14_out, and_15_out);
  or or_5 (f1, and_16_out, and_17_out);
  or or_6 (g1, and_18_out, and_19_out);
  or or_7 (a2, and_20_out, and_21_out, and_22_out, and_23_out, and_24_out, and_25_out, and_26_out, and_27_out, and_28_out, and_29_out, and_30_out);
  or or_8 (c2, D, and_46_out, and_47_out, and_48_out, and_49_out, and_50_out, and_51_out, and_52_out, and_53_out);
  or or_9 (e2, and_67_out, and_68_out, and_69_out, and_70_out, and_71_out, and_72_out, and_73_out, and_74_out);
  or or_10 (f2, and_75_out, and_76_out, and_77_out, and_78_out, and_79_out, and_80_out, and_81_out, and_82_out);
  or or_11 (g2, and_83_out, and_84_out, and_85_out, and_86_out, and_87_out, and_88_out, and_89_out);
  or or_12 (b2, and_31_out, and_32_out, and_33_out, and_34_out, and_35_out, and_36_out, and_37_out, and_38_out, and_39_out, and_40_out, and_41_out, and_42_out, and_43_out, and_44_out, and_45_out);
  or or_13 (d2, and_54_out, and_55_out, and_56_out, and_57_out, and_58_out, and_59_out, and_60_out, and_61_out, and_62_out, and_63_out, and_64_out, and_65_out, and_66_out);

  assign b1 = 1'b1;
endmodule

module Bai02 (
  input  [3:0] A,
  input  in_2,
  input  [3:0] B
);

  wire bai_1_a1, bai_1_a2, bai_1_b1, bai_1_b2, bai_1_c1, bai_1_c2, bai_1_d1, bai_1_d2, bai_1_e1, bai_1_e2,
       bai_1_f1, bai_1_f2, bai_1_g1, bai_1_g2, bai_2_a1, bai_2_a2, bai_2_b1, bai_2_b2, bai_2_c1, bai_2_c2,
       bai_2_d1, bai_2_d2, bai_2_e1, bai_2_e2, bai_2_f1, bai_2_f2, bai_2_g1, bai_2_g2, bai_3_a1, bai_3_a2,
       bai_3_b1, bai_3_b2, bai_3_c1, bai_3_c2, bai_3_d1, bai_3_d2, bai_3_e1, bai_3_e2, bai_3_f1, bai_3_f2,
       bai_3_g1, bai_3_g2, machcong_1_c1, machcong_1_s, machcong_2_c1, machcong_2_s, machcong_3_c1,
       machcong_3_s, machcong_4_c1, machcong_4_s;

  Bai bai_1 (
    .A(A[3]), .B(A[2]), .C(A[1]), .D(A[0]), .a1(bai_1_a1), .b1(bai_1_b1), .c1(bai_1_c1), .d1(bai_1_d1),
    .e1(bai_1_e1), .f1(bai_1_f1), .g1(bai_1_g1), .a2(bai_1_a2), .b2(bai_1_b2), .c2(bai_1_c2), .d2(bai_1_d2),
    .e2(bai_1_e2), .f2(bai_1_f2), .g2(bai_1_g2));  // open: E
  _7_Segment_Display u_7_segment_display_1 (
    .g(bai_1_g1), .f(bai_1_f1), .a(bai_1_a1), .b(bai_1_b1), .e(bai_1_e1), .d(bai_1_d1), .c(bai_1_c1));  // open: dp
  _7_Segment_Display u_7_segment_display_2 (
    .g(bai_1_g2), .f(bai_1_f2), .a(bai_1_a2), .b(bai_1_b2), .e(bai_1_e2), .d(bai_1_d2), .c(bai_1_c2));  // open: dp
  Bai bai_2 (
    .A(B[3]), .B(B[2]), .C(B[1]), .D(B[0]), .a1(bai_2_a1), .b1(bai_2_b1), .c1(bai_2_c1), .d1(bai_2_d1),
    .e1(bai_2_e1), .f1(bai_2_f1), .g1(bai_2_g1), .a2(bai_2_a2), .b2(bai_2_b2), .c2(bai_2_c2), .d2(bai_2_d2),
    .e2(bai_2_e2), .f2(bai_2_f2), .g2(bai_2_g2));  // open: E
  _7_Segment_Display u_7_segment_display_3 (
    .g(bai_2_g1), .f(bai_2_f1), .a(bai_2_a1), .b(bai_2_b1), .e(bai_2_e1), .d(bai_2_d1), .c(bai_2_c1));  // open: dp
  _7_Segment_Display u_7_segment_display_4 (
    .g(bai_2_g2), .f(bai_2_f2), .a(bai_2_a2), .b(bai_2_b2), .e(bai_2_e2), .d(bai_2_d2), .c(bai_2_c2));  // open: dp
  Machcong machcong_1 (.A(A[0]), .B(B[0]), .C0(in_2), .S(machcong_1_s), .C1(machcong_1_c1));
  Machcong machcong_2 (.A(A[1]), .B(B[1]), .C0(machcong_1_c1), .S(machcong_2_s), .C1(machcong_2_c1));
  Machcong machcong_3 (.A(A[2]), .B(B[2]), .C0(machcong_2_c1), .S(machcong_3_s), .C1(machcong_3_c1));
  Machcong machcong_4 (.A(A[3]), .B(B[3]), .C0(machcong_3_c1), .S(machcong_4_s), .C1(machcong_4_c1));
  Bai bai_3 (
    .E(machcong_4_c1), .A(machcong_4_s), .B(machcong_3_s), .C(machcong_2_s), .D(machcong_1_s), .a1(bai_3_a1),
    .b1(bai_3_b1), .c1(bai_3_c1), .d1(bai_3_d1), .e1(bai_3_e1), .f1(bai_3_f1), .g1(bai_3_g1), .a2(bai_3_a2),
    .b2(bai_3_b2), .c2(bai_3_c2), .d2(bai_3_d2), .e2(bai_3_e2), .f2(bai_3_f2), .g2(bai_3_g2));
  _7_Segment_Display u_7_segment_display_5 (
    .g(bai_3_g1), .f(bai_3_f1), .a(bai_3_a1), .b(bai_3_b1), .e(bai_3_e1), .d(bai_3_d1), .c(bai_3_c1));  // open: dp
  _7_Segment_Display u_7_segment_display_6 (
    .g(bai_3_g2), .f(bai_3_f2), .a(bai_3_a2), .b(bai_3_b2), .e(bai_3_e2), .d(bai_3_d2), .c(bai_3_c2));  // open: dp
endmodule

module Machcong (
  input  A,
  input  B,
  input  C0,
  output S,
  output C1
);

  wire and_1_out, and_2_out, and_3_out, and_4_out, and_5_out, and_6_out, and_7_out, not_1_out, not_2_out,
       not_3_out;

  not not_1 (not_1_out, A);
  not not_2 (not_2_out, B);
  not not_3 (not_3_out, C0);
  and and_1 (and_1_out, not_1_out, not_2_out, C0);
  and and_2 (and_2_out, not_1_out, B, not_3_out);
  and and_3 (and_3_out, A, not_2_out, not_3_out);
  and and_4 (and_4_out, A, B, C0);
  and and_5 (and_5_out, B, C0);
  and and_6 (and_6_out, A, C0);
  and and_7 (and_7_out, A, B);
  or or_1 (S, and_1_out, and_2_out, and_3_out, and_4_out);
  or or_2 (C1, and_5_out, and_6_out, and_7_out);
endmodule

module Bai1 (
  input  A,
  input  B,
  input  S0,
  input  C,
  input  S1,
  input  D,
  output F
);

  wire multiplexer_1_out, multiplexer_2_out;

  Multiplexer multiplexer_1 (.in0(A), .in1(B), .out(multiplexer_1_out), .sel(S0));
  Multiplexer multiplexer_2 (.in0(C), .in1(D), .out(multiplexer_2_out), .sel(S0));
  Multiplexer multiplexer_3 (.in0(multiplexer_1_out), .in1(multiplexer_2_out), .out(F), .sel(S1));
endmodule
