// Logisim project la42.circ as structural Verilog: 3 circuits, main circuit main
module main (
  input  A0,
  input  B0,
  input  A1,
  input  B1,
  input  A2,
  input  B2,
  input  A3,
  input  B3,
  output S0,
  output S1,
  output S2,
  output S3,
  output S4
);

  wire adder_1_cout, adder_2_cout, adder_3_cout, in1_a, in1_a1, in1_b, in1_b1, in1_c, in1_c1, in1_d, in1_d1,
       in1_e, in1_e1, in1_f, in1_f1, in1_g, in1_g1, in2_a, in2_a1, in2_b, in2_b1, in2_c, in2_c1, in2_d,
       in2_d1, in2_e, in2_e1, in2_f, in2_f1, in2_g, in2_g1, out0_a, out0_a1, out0_b, out0_b1, out0_c,
       out0_c1, out0_d, out0_d1, out0_e, out0_e1, out0_f, out0_f1, out0_g, out0_g1;

  Adder #(.width(1)) adder_1 (.a(A0), .b(B0), .out(S0), .cout(adder_1_cout));  // open: cin
  Adder #(.width(1)) adder_2 (.a(A1), .b(B1), .out(S1), .cin(adder_1_cout), .cout(adder_2_cout));
  Adder #(.width(1)) adder_3 (.a(A2), .b(B2), .out(S2), .cin(adder_2_cout), .cout(adder_3_cout));
  Adder #(.width(1)) adder_4 (.a(A3), .b(B3), .out(S3), .cin(adder_3_cout), .cout(S4));
  LED_IN in2 (
    .I3(B3), .I2(B2), .I1(B1), .I0(B0), .A(in2_a), .B(in2_b), .C(in2_c), .D(in2_d), .E(in2_e), .F(in2_f),
    .G(in2_g), .A1(in2_a1), .B1(in2_b1), .C1(in2_c1), .D1(in2_d1), .E1(in2_e1), .F1(in2_f1), .G1(in2_g1));
  LED_IN in1 (
    .I3(A3), .I2(A2), .I1(A1), .I0(A0), .A(in1_a), .B(in1_b), .C(in1_c), .D(in1_d), .E(in1_e), .F(in1_f),
    .G(in1_g), .A1(in1_a1), .B1(in1_b1), .C1(in1_c1), .D1(in1_d1), .E1(in1_e1), .F1(in1_f1), .G1(in1_g1));
  _7_Segment_Display u_7_segment_display_1 (
    .g(in2_g1), .f(in2_f1), .a(in2_a1), .b(in2_b1), .e(in2_e1), .d(in2_d1), .c(in2_c1));  // open: dp
  _7_Segment_Display #(.decimalPoint("false")) u_7_segment_display_2 (
    .g(in2_g), .f(in2_f), .a(in2_a), .b(in2_b), .e(in2_e), .d(in2_d), .c(in2_c));
  _7_Segment_Display u_7_segment_display_3 (
    .g(in1_g1), .f(in1_f1), .a(in1_a1), .b(in1_b1), .e(in1_e1), .d(in1_d1), .c(in1_c1));  // open: dp
  _7_Segment_Display #(.decimalPoint("false")) u_7_segment_display_4 (
    .g(in1_g), .f(in1_f), .a(in1_a), .b(in1_b), .e(in1_e), .d(in1_d), .c(in1_c));
  LED_OUT out0 (
    .I4(S4), .I3(S3), .I2(S2), .I1(S1), .I0(S0), .A(out0_a), .B(out0_b), .C(out0_c), .D(out0_d), .E(out0_e),
    .F(out0_f), .G(out0_g), .A1(out0_a1), .B1(out0_b1), .C1(out0_c1), .D1(out0_d1), .E1(out0_e1),
    .F1(out0_f1), .G1(out0_g1));
  _7_Segment_Display u_7_segment_display_5 (
    .g(out0_g1), .f(out0_f1), .a(out0_a1), .b(out0_b1), .e(out0_e1), .d(out0_d1), .c(out0_c1));  // open: dp
  _7_Segment_Display #(.decimalPoint("false")) u_7_segment_display_6 (
    .g(out0_g), .f(out0_f), .a(out0_a), .b(out0_b), .e(out0_e), .d(out0_d), .c(out0_c));
endmodule

module LED_IN (
  input  I3,
  input  I2,
  input  I1,
  input  I0,
  output A,
  output B,
  output C,
  output D,
  output E,
  output F,
  output G,
  output A1,
  output B1,
  output C1,
  output D1,
  output E1,
  output F1,
  output G1
);

  wire and_1_out, and_2_out, and_3_out, and_4_out, and_5_out, and_6_out, and_7_out, and_8_out, and_9_out,
       and_10_out, and_11_out, and_12_out, and_13_out, and_14_out, and_15_out, and_16_out, and_17_out,
       and_18_out, and_19_out, and_20_out, and_21_out, and_22_out, and_23_out, and_24_out, and_25_out,
       and_26_out, and_27_out, and_28_out, and_29_out, and_30_out, and_31_out, and_32_out, and_33_out,
       and_34_out, and_35_out, and_36_out, and_37_out, not_1_out, not_2_out, not_3_out, not_4_out;

  not not_1 (not_1_out, I3);
  not not_2 (not_2_out, I2);
  not not_3 (not_3_out, I1);
  not not_4 (not_4_out, I0);
  and and_1 (and_1_out, not_2_out, not_4_out);
  and and_2 (and_2_out, not_1_out, I1);
  and and_3 (and_3_out, I2, I0);
  and and_4 (and_4_out, I3, not_3_out);
  and and_5 (and_5_out, not_3_out, not_4_out);
  and and_6 (and_6_out, not_1_out, I1, I0);
  and and_7 (and_7_out, I3, not_3_out);
  and and_8 (and_8_out, I3, not_4_out);
  and and_9 (and_9_out, not_1_out, not_3_out);
  and and_10 (and_10_out, not_1_out, I2);
  and and_11 (and_11_out, not_2_out, not_3_out);
  and and_12 (and_12_out, I3, not_2_out);
  and and_13 (and_13_out, I2, I1);
  and and_14 (and_14_out, not_2_out, not_4_out);
  and and_15 (and_15_out, not_1_out, not_2_out, I1);
  and and_16 (and_16_out, I2, not_3_out, I0);
  and and_17 (and_17_out, not_1_out, I1, not_4_out);
  and and_18 (and_18_out, I3, not_3_out);
  and and_19 (and_19_out, I3, I2, I0);
  and and_20 (and_20_out, not_2_out, not_4_out);
  and and_21 (and_21_out, not_1_out, I1, not_4_out);
  and and_22 (and_22_out, I3, not_3_out, not_4_out);
  and and_23 (and_23_out, not_1_out, I2, not_3_out);
  and and_24 (and_24_out, I3, not_2_out, not_3_out);
  and and_25 (and_25_out, I3, I2, I1);
  and and_26 (and_26_out, not_1_out, not_3_out, not_4_out);
  and and_27 (and_27_out, not_1_out, I2, not_4_out);
  and and_28 (and_28_out, I3, not_2_out, not_4_out);
  and and_29 (and_29_out, not_1_out, not_2_out, I1);
  and and_30 (and_30_out, I2, not_3_out);
  and and_31 (and_31_out, I3, not_3_out);
  and and_32 (and_32_out, I3, I2);
  and and_33 (and_33_out, not_1_out, I1, not_4_out);
  and and_34 (and_34_out, not_2_out, not_3_out);
  and and_35 (and_35_out, not_2_out, not_3_out);
  and and_36 (and_36_out, not_2_out, not_3_out);
  and and_37 (and_37_out, not_2_out, not_3_out);
  or or_1 (A, and_1_out, and_2_out, and_3_out, and_4_out);
  or or_2 (B, not_2_out, and_5_out, and_6_out, and_7_out, and_8_out);
  or or_3 (C, I0, and_9_out, and_10_out, and_11_out, and_12_out, and_13_out);
  or or_4 (D, and_14_out, and_15_out, and_16_out, and_17_out, and_18_out, and_19_out);
  or or_5 (E, and_20_out, and_21_out, and_22_out);
  or or_6 (F, and_23_out, and_24_out, and_25_out, and_26_out, and_27_out, and_28_out);
  or or_7 (G, and_29_out, and_30_out, and_31_out, and_32_out, and_33_out);
  or or_8 (A1, not_1_out, and_34_out);
  or or_9 (D1, not_1_out, and_35_out);
  or or_10 (E1, not_1_out, and_36_out);
  or or_11 (F1, not_1_out, and_37_out);

  assign B1 = 1'b1;
  assign C1 = 1'b1;
  assign G1 = 1'b0;
endmodule

module LED_OUT (
  input  I4,
  input  I3,
  input  I2,
  input  I1,
  input  I0,
  output A,
  output B,
  output C,
  output D,
  output E,
  output F,
  output G,
  output A1,
  output B1,
  output C1,
  output D1,
  output E1,
  output F1,
  output G1
);

  wire and_1_out, and_2_out, and_3_out, and_4_out, and_5_out, and_6_out, and_7_out, and_8_out, and_9_out,
       and_10_out, and_11_out, and_12_out, and_13_out, and_14_out, and_15_out, and_16_out, and_17_out,
       and_18_out, and_19_out, and_20_out, and_21_out, and_22_out, and_23_out, and_24_out, and_25_out,
       and_26_out, and_27_out, and_28_out, and_29_out, and_30_out, and_31_out, and_32_out, and_33_out,
       and_34_out, and_35_out, and_36_out, and_37_out, and_38_out, and_39_out, and_40_out, and_41_out,
       and_42_out, and_43_out, and_44_out, and_45_out, and_46_out, and_47_out, and_48_out, and_49_out,
       and_50_out, and_51_out, and_52_out, and_53_out, and_54_out, and_55_out, and_56_out, and_57_out,
       and_58_out, and_59_out, and_60_out, and_61_out, and_62_out, and_63_out, and_64_out, and_65_out,
       and_66_out, and_67_out, and_68_out, and_69_out, and_70_out, and_71_out, and_72_out, and_73_out,
       and_74_out, and_75_out, and_76_out, and_77_out, and_78_out, and_79_out, and_80_out, and_81_out,
       and_82_out, and_83_out, and_84_out, and_85_out, and_86_out, and_87_out, and_88_out, and_89_out,
       and_90_out, and_91_out, and_92_out, and_93_out, and_94_out, and_95_out, and_96_out, and_97_out,
       not_1_out, not_2_out, not_3_out, not_4_out, not_5_out;

  not not_1 (not_1_out, I4);
  not not_2 (not_2_out, I3);
  not not_3 (not_3_out, I2);
  not not_4 (not_4_out, I1);
  not not_5 (not_5_out, I0);
  and and_1 (and_1_out, not_2_out, I1);
  and and_2 (and_2_out, not_1_out, I2, I0);
  and and_3 (and_3_out, not_1_out, not_3_out, not_5_out);
  and and_4 (and_4_out, not_1_out, I3, not_4_out);
  and and_5 (and_5_out, not_2_out, not_3_out, not_5_out);
  and and_6 (and_6_out, I4, not_2_out, not_3_out);
  and and_7 (and_7_out, I4, not_2_out, not_5_out);
  and and_8 (and_8_out, I4, not_3_out, I0);
  and and_9 (and_9_out, not_3_out, I1, not_5_out);
  and and_10 (and_10_out, I3, I2, not_4_out);
  and and_11 (and_11_out, I4, I2, not_5_out);
  and and_12 (and_12_out, not_2_out, I1, I0);
  and and_13 (and_13_out, I3, not_4_out, not_5_out);
  and and_14 (and_14_out, not_3_out, I1, I0);
  and and_15 (and_15_out, not_1_out, not_3_out);
  and and_16 (and_16_out, not_1_out, not_4_out, not_5_out);
  and and_17 (and_17_out, not_1_out, I3, not_4_out);
  and and_18 (and_18_out, not_1_out, I3, not_5_out);
  and and_19 (and_19_out, not_2_out, not_3_out, I0);
  and and_20 (and_20_out, not_2_out, not_3_out, I1);
  and and_21 (and_21_out, I2, not_4_out, not_5_out);
  and and_22 (and_22_out, I4, not_2_out, I0);
  and and_23 (and_23_out, I4, not_2_out, I1);
  and and_24 (and_24_out, I3, I2, not_4_out);
  and and_25 (and_25_out, I3, I2, not_5_out);
  and and_26 (and_26_out, I4, not_3_out);
  and and_27 (and_27_out, not_2_out, not_4_out);
  and and_28 (and_28_out, not_1_out, not_2_out, I2);
  and and_29 (and_29_out, not_3_out, not_4_out);
  and and_30 (and_30_out, I3, not_3_out);
  and and_31 (and_31_out, not_1_out, I2, I1);
  and and_32 (and_32_out, I4, not_4_out);
  and and_33 (and_33_out, I3, I1);
  and and_34 (and_34_out, not_2_out, not_3_out, I1);
  and and_35 (and_35_out, not_1_out, I2, not_4_out, I0);
  and and_36 (and_36_out, not_2_out, I1, not_5_out);
  and and_37 (and_37_out, I3, I2, I0);
  and and_38 (and_38_out, I3, not_4_out, I0);
  and and_39 (and_39_out, I4, I2, I1);
  and and_40 (and_40_out, not_3_out, I1, not_5_out);
  and and_41 (and_41_out, not_1_out, not_3_out, not_5_out);
  and and_42 (and_42_out, not_1_out, I3, not_4_out);
  and and_43 (and_43_out, not_2_out, not_3_out, not_5_out);
  and and_44 (and_44_out, I4, not_2_out, not_5_out);
  and and_45 (and_45_out, I3, I2, not_4_out);
  and and_46 (and_46_out, not_2_out, I1, not_5_out);
  and and_47 (and_47_out, not_2_out, not_3_out, not_5_out);
  and and_48 (and_48_out, not_1_out, not_3_out, not_5_out);
  and and_49 (and_49_out, not_1_out, I3, not_4_out, not_5_out);
  and and_50 (and_50_out, I4, not_2_out, not_5_out);
  and and_51 (and_51_out, not_3_out, I1, not_5_out);
  and and_52 (and_52_out, I3, I2, not_4_out, not_5_out);
  and and_53 (and_53_out, I4, I1, not_5_out);
  and and_54 (and_54_out, not_1_out, not_2_out, I2, not_4_out);
  and and_55 (and_55_out, I3, not_3_out, not_4_out);
  and and_56 (and_56_out, not_1_out, I3, I2, I1);
  and and_57 (and_57_out, I4, not_2_out, not_3_out, I1);
  and and_58 (and_58_out, I4, I3, not_4_out);
  and and_59 (and_59_out, not_2_out, not_4_out, not_5_out);
  and and_60 (and_60_out, I3, I1, not_5_out);
  and and_61 (and_61_out, not_1_out, not_2_out, I2, not_5_out);
  and and_62 (and_62_out, not_2_out, not_3_out, I1);
  and and_63 (and_63_out, not_1_out, I2, not_4_out);
  and and_64 (and_64_out, I3, not_4_out);
  and and_65 (and_65_out, I4, not_3_out, not_5_out);
  and and_66 (and_66_out, not_2_out, I1, not_5_out);
  and and_67 (and_67_out, not_1_out, I2, not_5_out);
  and and_68 (and_68_out, not_1_out, I3, I2);
  and and_69 (and_69_out, I4, not_2_out, I1);
  and and_70 (and_70_out, I4, I2, I1, I0);
  and and_71 (and_71_out, not_1_out, not_2_out);
  and and_72 (and_72_out, I2, not_5_out);
  and and_73 (and_73_out, I4, I3);
  and and_74 (and_74_out, not_1_out, not_3_out, not_4_out);
  and and_75 (and_75_out, not_2_out, I2);
  and and_76 (and_76_out, not_2_out, not_3_out);
  and and_77 (and_77_out, I3, I2, I1);
  and and_78 (and_78_out, not_1_out, not_2_out);
  and and_79 (and_79_out, I2, not_5_out);
  and and_80 (and_80_out, I4, I3);
  and and_81 (and_81_out, not_1_out, not_3_out, not_4_out);
  and and_82 (and_82_out, not_2_out, I2);
  and and_83 (and_83_out, not_1_out, not_2_out);
  and and_84 (and_84_out, not_1_out, I2, not_5_out);
  and and_85 (and_85_out, not_2_out, I2);
  and and_86 (and_86_out, I4, I3, not_3_out);
  and and_87 (and_87_out, not_1_out, not_3_out, not_4_out);
  and and_88 (and_88_out, I3, not_4_out, not_5_out);
  and and_89 (and_89_out, I4, I2, not_4_out);
  and and_90 (and_90_out, I4, I2, I0);
  and and_91 (and_91_out, not_1_out, not_2_out);
  and and_92 (and_92_out, not_1_out, not_3_out, not_4_out);
  and and_93 (and_93_out, not_1_out, I2, not_5_out);
  and and_94 (and_94_out, I4, not_2_out, I2);
  and and_95 (and_95_out, I4, I3, not_3_out);
  and and_96 (and_96_out, I4, I2, not_4_out);
  and and_97 (and_97_out, I4, I2, not_5_out);
  or or_1 (C, I0, and_26_out, and_27_out, and_28_out, and_29_out, and_30_out, and_31_out, and_32_out, and_33_out);
  or or_2 (E, and_46_out, and_47_out, and_48_out, and_49_out, and_50_out, and_51_out, and_52_out, and_53_out);
  or or_3 (F, and_54_out, and_55_out, and_56_out, and_57_out, and_58_out, and_59_out, and_60_out, and_61_out);
  or or_4 (G, and_62_out, and_63_out, and_64_out, and_65_out, and_66_out, and_67_out, and_68_out, and_69_out, and_70_out);
  or or_5 (A1, and_71_out, and_72_out, and_73_out, and_74_out, and_75_out);
  or or_6 (C1, not_1_out, and_76_out, and_77_out);
  or or_7 (D1, and_78_out, and_79_out, and_80_out, and_81_out, and_82_out);
  or or_8 (E1, and_83_out, and_84_out, and_85_out, and_86_out, and_87_out, and_88_out, and_89_out, and_90_out);
  or or_9 (F1, and_91_out, and_92_out, and_93_out);
  or or_10 (G1, and_94_out, and_95_out, and_96_out, and_97_out);
  or or_11 (A, and_1_out, and_2_out, and_3_out, and_4_out, and_5_out, and_6_out, and_7_out, and_8_out, and_9_out, and_10_out, and_11_out);
  or or_12 (B, and_12_out, and_13_out, and_14_out, and_15_out, and_16_out, and_17_out, and_18_out, and_19_out, and_20_out, and_21_out, and_22_out, and_23_out, and_24_out, and_25_out);
  or or_13 (D, and_34_out, and_35_out, and_36_out, and_37_out, and_38_out, and_39_out, and_40_out, and_41_out, and_42_out, and_43_out, and_44_out, and_45_out);

  assign B1 = 1'b1;
endmodule
