// Logisim project Bai1.circ as structural Verilog: 2 circuits, main circuit test
module main (
  output Y
);

  wire CLKA_out, CLKB_out;

  Clock #(.highDuration(2), .lowDuration(2)) CLKB (.out(CLKB_out));
  Clock CLKA (.out(CLKA_out));
  test test_1 (.A(CLKA_out), .B(CLKB_out), .Y(Y));
endmodule

module test (
  input  A,
  input  B,
  output Y
);

  wire and_1_out, and_2_out, not_1_out, not_2_out;

  not not_1 (not_1_out, B);
  not not_2 (not_2_out, A);
  and and_1 (and_1_out, A, not_1_out);
  and and_2 (and_2_out, not_2_out, B);
  or or_1 (Y, and_1_out, and_2_out);
endmodule
