// Logisim project Bai2.circ as structural Verilog: 2 circuits, main circuit main
module main (
  output Y
);

  wire A_out, B_out, S_out;

  Clock #(.highDuration(4), .lowDuration(4)) S (.out(S_out));
  Clock A (.out(A_out));
  Clock #(.highDuration(2), .lowDuration(2)) B (.out(B_out));
  test test_1 (.S(S_out), .A(A_out), .B(B_out), .Y(Y));
endmodule

module test (
  input  S,
  input  A,
  input  B,
  output Y
);

  wire and_1_out, and_2_out, not_1_out;

  not not_1 (not_1_out, S);
  and and_1 (and_1_out, S, A);
  and and_2 (and_2_out, not_1_out, B);
  or or_1 (Y, and_1_out, and_2_out);
endmodule
