// Logisim project CAU2.circ as structural Verilog: 3 circuits, main circuit main
module main (
  output LEDR0,
  output LEDR2,
  output LEDR4,
  output LEDR6,
  output LEDR8
);

  wire SW0_out, SW1_out;

  Clock SW0 (.out(SW0_out));
  Clock #(.highDuration(2), .lowDuration(2)) SW1 (.out(SW1_out));
  Test test_1 (.SW0(SW0_out), .SW1(SW1_out), .LEDR0(LEDR0), .LEDR2(LEDR2), .LEDR4(LEDR4), .LEDR6(LEDR6), .LEDR8(LEDR8));
endmodule

module Test (
  input  SW0,
  input  SW1,
  output LEDR0,
  output LEDR2,
  output LEDR4,
  output LEDR6,
  output LEDR8
);

  and and_1 (LEDR0, SW0, SW1);
  or or_1 (LEDR2, SW0, SW1);
  nand nand_1 (LEDR4, SW0, SW1);
  nor nor_1 (LEDR6, SW0, SW1);
  not not_1 (LEDR8, SW0);
endmodule

module Test2 (
  output L0,
  output L2,
  output L4,
  output L6,
  output L8
);

  wire S0_out, S1_out;

  Clock S0 (.out(S0_out));
  Clock #(.highDuration(2), .lowDuration(2)) S1 (.out(S1_out));
  Test test_1 (.SW0(S0_out), .SW1(S1_out), .LEDR0(L0), .LEDR2(L2), .LEDR4(L4), .LEDR6(L6), .LEDR8(L8));
endmodule
