// Logisim project CAU3.circ as structural Verilog: 2 circuits, main circuit main
module main (
  output LEDG0
);

  wire SW0_out, SW1_out;

  Clock #(.highDuration(2), .lowDuration(2)) SW0 (.out(SW0_out));
  Clock SW1 (.out(SW1_out));
  Test test_1 (.A(SW0_out), .B(SW1_out), .Y1(LEDG0));  // open: Y2
endmodule

module Test (
  input  A,
  input  B,
  output Y1,
  output Y2
);

  nand nand_1 (Y1, A, B);
  nand nand_2 (Y2, Y1, Y1);
endmodule
