// Logisim project LAB02DT_EXERCISE.circ as structural Verilog: 8 circuits, main circuit main
module main (
  input  A,
  input  B,
  input  C,
  input  D,
  output F1
);

  wire and_1_out, and_2_out, and_3_out, and_4_out, not_1_out, not_2_out, not_3_out, not_4_out, not_5_out;

  not not_1 (not_1_out, A);
  not not_2 (not_2_out, B);
  not not_3 (not_3_out, D);
  not not_4 (not_4_out, A);
  not not_5 (not_5_out, C);
  and and_1 (and_1_out, not_4_out, B, not_5_out, D);
  and and_2 (and_2_out, not_1_out, not_2_out, C);
  and and_3 (and_3_out, A, not_3_out, B);
  and and_4 (and_4_out, B, C, D);
  or or_1 (F1, and_1_out, and_2_out, and_3_out, and_4_out);
endmodule

module main2 (
  output F1
);

  wire A_out, B_out, C_out, D_out;

  Clock #(.highDuration(8), .lowDuration(8)) A (.out(A_out));
  Clock #(.highDuration(4), .lowDuration(4)) B (.out(B_out));
  Clock #(.highDuration(2), .lowDuration(2)) C (.out(C_out));
  Clock D (.out(D_out));
  main main_1 (.A(A_out), .B(B_out), .C(C_out), .D(D_out), .F1(F1));
endmodule

module c3test (
  input  A,
  input  B,
  input  C,
  input  D,
  output F2
);

  wire not_1_out, not_2_out, not_3_out, not_4_out, not_5_out, or_1_out, or_2_out, or_3_out, or_4_out;

  not not_1 (not_1_out, D);
  not not_2 (not_2_out, A);
  not not_3 (not_3_out, B);
  not not_4 (not_4_out, A);
  not not_5 (not_5_out, C);
  or or_1 (or_1_out, A, B, not_1_out);
  or or_2 (or_2_out, not_2_out, not_3_out, C);
  or or_3 (or_3_out, B, C, D);
  or or_4 (or_4_out, not_4_out, B, not_5_out, D);
  and and_1 (F2, or_1_out, or_2_out, or_3_out, or_4_out);
endmodule

module c3main (
  output F2
);

  wire A_out, B_out, C_out, D_out;

  Clock D (.out(D_out));
  Clock #(.highDuration(2), .lowDuration(2)) C (.out(C_out));
  Clock #(.highDuration(4), .lowDuration(4)) B (.out(B_out));
  Clock #(.highDuration(8), .lowDuration(8)) A (.out(A_out));
  c3test c3test_1 (.A(A_out), .B(B_out), .C(C_out), .D(D_out), .F2(F2));
endmodule

module c5test (
  input  A,
  input  B,
  input  C,
  input  D,
  output F3
);

  wire and_1_out, and_2_out, and_3_out, and_4_out, not_1_out, not_2_out, not_3_out, not_4_out;

  not not_1 (not_1_out, A);
  not not_2 (not_2_out, B);
  not not_3 (not_3_out, A);
  not not_4 (not_4_out, D);
  and and_1 (and_1_out, not_1_out, not_2_out, C);
  and and_2 (and_2_out, not_3_out, B, D);
  and and_3 (and_3_out, B, C, D);
  and and_4 (and_4_out, A, B, not_4_out);
  or or_1 (F3, and_1_out, and_2_out, and_3_out, and_4_out);
endmodule

module c5main (
  output F3
);

  wire A_out, B_out, C_out, D_out;

  Clock D (.out(D_out));
  Clock #(.highDuration(2), .lowDuration(2)) C (.out(C_out));
  Clock #(.highDuration(4), .lowDuration(4)) B (.out(B_out));
  Clock #(.highDuration(8), .lowDuration(8)) A (.out(A_out));
  c5test c5test_1 (.A(A_out), .B(B_out), .C(C_out), .D(D_out), .F3(F3));
endmodule

module c6test (
  input  A,
  input  B,
  input  C,
  input  D,
  output F2
);

  wire and_1_out, and_2_out, and_3_out, and_4_out, not_1_out, not_2_out, not_3_out;

  not not_1 (not_1_out, A);
  not not_2 (not_2_out, D);
  not not_3 (not_3_out, B);
  and and_1 (and_1_out, not_1_out, C, not_2_out);
  and and_2 (and_2_out, not_1_out, B);
  and and_3 (and_3_out, A, not_3_out, D);
  and and_4 (and_4_out, B, C);
  or or_1 (F2, and_1_out, and_2_out, and_3_out, and_4_out);
endmodule

module c6main (
  output F2
);

  wire A_out, B_out, C_out, D_out;

  Clock D (.out(D_out));
  Clock #(.highDuration(2), .lowDuration(2)) C (.out(C_out));
  Clock #(.highDuration(4), .lowDuration(4)) B (.out(B_out));
  Clock #(.highDuration(8), .lowDuration(8)) A (.out(A_out));
  c6test c6test_1 (.A(A_out), .B(B_out), .C(C_out), .D(D_out), .F2(F2));
endmodule
