// Logisim project LAB02DT_LAB.circ as structural Verilog: 4 circuits, main circuit c1test
module c1test (
  input  A,
  input  B,
  input  C,
  input  D,
  output F1
);

  wire and_1_out, and_2_out, and_3_out, not_1_out, not_2_out;

  not not_1 (not_1_out, A);
  not not_2 (not_2_out, B);
  and and_1 (and_1_out, not_1_out, C, D);
  and and_2 (and_2_out, A, B);
  and and_3 (and_3_out, A, not_2_out);
  or or_1 (F1, and_1_out, and_2_out, and_3_out);
endmodule

module c1main (
  output F1
);

  wire A_out, B_out, C_out, D_out;

  Clock D (.out(D_out));
  Clock #(.highDuration(2), .lowDuration(2)) C (.out(C_out));
  Clock #(.highDuration(4), .lowDuration(4)) B (.out(B_out));
  Clock #(.highDuration(8), .lowDuration(8)) A (.out(A_out));
  c1test c1test_1 (.A(A_out), .B(B_out), .C(C_out), .D(D_out), .F1(F1));
endmodule

module c2test (
  input  A,
  input  B,
  input  C,
  input  D,
  output F1
);

  wire and_1_out;

  and and_1 (and_1_out, C, D);
  or or_1 (F1, A, and_1_out);
endmodule

module c2main (
  output F1
);

  wire A_out, C_out, D_out;

  Clock D (.out(D_out));
  Clock #(.highDuration(2), .lowDuration(2)) C (.out(C_out));
  Clock #(.highDuration(8), .lowDuration(8)) A (.out(A_out));
  c2test c2test_1 (.A(A_out), .C(C_out), .D(D_out), .F1(F1));  // open: B
endmodule
