// Logisim project LAB_3_EXERCISE.circ as structural Verilog
module LED_A (
  input  I3,
  input  I2,
  input  I1,
  input  I0,
  output A
);

  wire and_1_out, and_2_out, and_3_out, not_1_out, not_2_out, not_3_out, not_4_out, not_5_out;

  not not_1 (not_1_out, I1);
  not not_2 (not_2_out, I0);
  not not_3 (not_3_out, I3);
  not not_4 (not_4_out, I1);
  not not_5 (not_5_out, I2);
  and and_1 (and_1_out, I3, I1);
  and and_2 (and_2_out, I2, not_1_out, not_2_out);
  and and_3 (and_3_out, not_3_out, not_4_out, not_5_out, I0);
  or or_1 (A, and_1_out, and_2_out, and_3_out);
endmodule

module LED_B (
  input  I3,
  input  I2,
  input  I1,
  input  I0,
  output B
);

  wire and_1_out, and_2_out, xor_1_out;

  xor xor_1 (xor_1_out, I1, I0);
  and and_1 (and_1_out, I3, I1);
  and and_2 (and_2_out, I2, xor_1_out);
  or or_1 (B, and_1_out, and_2_out);
endmodule

module LED_C (
  input  I3,
  input  I2,
  input  I1,
  input  I0,
  output C
);

  wire and_1_out, and_2_out, not_1_out, not_2_out;

  not not_1 (not_1_out, I2);
  not not_2 (not_2_out, I0);
  and and_1 (and_1_out, I3, I1);
  and and_2 (and_2_out, not_1_out, I1, not_2_out);
  or or_1 (C, and_1_out, and_2_out);
endmodule

module LED_D (
  input  I3,
  input  I2,
  input  I1,
  input  I0,
  output D
);

  wire and_1_out, and_2_out, not_1_out, not_2_out, not_3_out, xnor_1_out;

  xnor xnor_1 (xnor_1_out, I1, I0);
  not not_1 (not_1_out, I1);
  not not_2 (not_2_out, I3);
  not not_3 (not_3_out, I2);
  and and_1 (and_1_out, I2, xnor_1_out);
  and and_2 (and_2_out, I0, not_1_out, not_2_out, not_3_out);
  or or_1 (D, and_2_out, and_1_out);
endmodule

module LED_E (
  input  I2,
  input  I1,
  input  I0,
  output E
);

  wire and_1_out, not_1_out, not_2_out;

  not not_1 (not_1_out, I1);
  not not_2 (not_2_out, I0);
  and and_1 (and_1_out, I2, not_1_out, not_2_out);
  or or_1 (E, and_1_out, I0);
endmodule

module LED_F (
  input  I3,
  input  I2,
  input  I1,
  input  I0,
  output F
);

  wire and_1_out, and_2_out, and_3_out, not_1_out, not_2_out;

  not not_1 (not_1_out, I3);
  not not_2 (not_2_out, I2);
  and and_1 (and_1_out, not_1_out, I0, not_2_out);
  and and_2 (and_2_out, not_2_out, I1);
  and and_3 (and_3_out, I1, I0);
  or or_1 (F, and_1_out, and_2_out, and_3_out);
endmodule

module LED_G (
  input  I3,
  input  I2,
  input  I1,
  input  I0,
  output G
);

  wire and_1_out, and_2_out, not_1_out, not_2_out, not_3_out;

  not not_1 (not_1_out, I3);
  not not_2 (not_2_out, I2);
  not not_3 (not_3_out, I1);
  and and_1 (and_1_out, I2, I3, I1, I0);
  and and_2 (and_2_out, not_1_out, not_2_out, not_3_out);
  or or_1 (G, and_1_out, and_2_out);
endmodule

module BCD_2_7_SEGMENT (
  input  I3,
  input  I2,
  input  I1,
  input  I0,
  output A,
  output B,
  output C,
  output D,
  output G,
  output E,
  output F
);

  LED_A led_a_1 (.I3(I3), .I2(I2), .I1(I1), .I0(I0), .A(A));
  LED_E led_e_1 (.I2(I2), .I1(I1), .I0(I0), .E(E));
  LED_B led_b_1 (.I3(I3), .I2(I2), .I1(I1), .I0(I0), .B(B));
  LED_F led_f_1 (.I3(I3), .I2(I2), .I1(I1), .I0(I0), .F(F));
  LED_C led_c_1 (.I3(I3), .I2(I2), .I1(I1), .I0(I0), .C(C));
  LED_G led_g_1 (.I3(I3), .I2(I2), .I1(I1), .I0(I0), .G(G));
  LED_D led_d_1 (.I3(I3), .I2(I2), .I1(I1), .I0(I0), .D(D));
endmodule

module BCD_2_7_SEGMENT_MAIN (
  output A,
  output B,
  output C,
  output D,
  output E,
  output F,
  output G
);

  wire I0_out, I1_out, I2_out, I3_out;

  Clock #(.highDuration(8), .lowDuration(8)) I3 (.out(I3_out));
  Clock #(.highDuration(4), .lowDuration(4)) I2 (.out(I2_out));
  Clock #(.highDuration(2), .lowDuration(2)) I1 (.out(I1_out));
  Clock I0 (.out(I0_out));
  BCD_2_7_SEGMENT bcd_2_7_segment_1 (
    .I3(I3_out), .I2(I2_out), .I1(I1_out), .I0(I0_out), .A(A), .B(B), .C(C), .D(D), .G(G), .E(E), .F(F));
endmodule
