// Logisim project LAB_3_LAB.circ as structural Verilog
module C1_LAB3_LAB (
  input  SW1,
  input  SW2,
  input  SW3,
  input  SW0,
  output HEX5,
  output HEX6,
  output HEX0,
  output HEX1,
  output HEX2,
  output HEX3,
  output HEX4
);

  wire n7447_1_pin3;

  _7447 #(.ShowInternalStructure("true")) u_7447_1 (
    .pin1(SW1), .pin2(SW2), .pin3(n7447_1_pin3), .pin4(n7447_1_pin3), .pin5(n7447_1_pin3), .pin6(SW3),
    .pin7(SW0), .pin15(HEX5), .pin14(HEX6), .pin13(HEX0), .pin12(HEX1), .pin11(HEX2), .pin10(HEX3),
    .pin9(HEX4));
  // also tied to VCC on the sheet: n7447_1_pin3
endmodule

module C1_LAB3_LAB_DGOI (
  input  SW0,
  input  SW3,
  input  SW2,
  input  SW1
);

  wire c1_lab3_lab_1_hex0, c1_lab3_lab_1_hex1, c1_lab3_lab_1_hex2, c1_lab3_lab_1_hex3, c1_lab3_lab_1_hex4,
       c1_lab3_lab_1_hex5, c1_lab3_lab_1_hex6;

  C1_LAB3_LAB c1_lab3_lab_1 (
    .SW1(SW1), .SW2(SW2), .SW3(SW3), .SW0(SW0), .HEX5(c1_lab3_lab_1_hex5), .HEX6(c1_lab3_lab_1_hex6),
    .HEX0(c1_lab3_lab_1_hex0), .HEX1(c1_lab3_lab_1_hex1), .HEX2(c1_lab3_lab_1_hex2),
    .HEX3(c1_lab3_lab_1_hex3), .HEX4(c1_lab3_lab_1_hex4));
  _7_Segment_Display LED (
    .g(c1_lab3_lab_1_hex5), .f(c1_lab3_lab_1_hex6), .a(c1_lab3_lab_1_hex0), .b(c1_lab3_lab_1_hex1),
    .e(c1_lab3_lab_1_hex4), .d(c1_lab3_lab_1_hex3), .c(c1_lab3_lab_1_hex2));  // open: dp
endmodule
