// Logisim project EXERCISE.circ as structural Verilog
module MUX_2_TO_1_1BIT (
  input  A,
  input  B,
  input  S,
  output Y
);

  wire and_1_out, and_2_out, not_1_out;

  not not_1 (not_1_out, S);
  and and_1 (and_1_out, A, S);
  and and_2 (and_2_out, B, not_1_out);
  or or_1 (Y, and_1_out, and_2_out);
endmodule

module MUX2_2BIT (
  input  A,
  input  B,
  input  S,
  output Y
);

  MUX_2_TO_1_1BIT mux_2_to_1_1bit_1 (.A(A), .B(B), .S(S), .Y(Y));
  MUX_2_TO_1_1BIT mux_2_to_1_1bit_2 (.A(A), .B(B), .S(S), .Y(Y));
endmodule

module MACH_SO_SANH (
  input  A,
  input  B,
  output GT,
  output EQ,
  output LT
);

  wire not_1_out, not_2_out, or_1_out;

  not not_1 (not_1_out, A);
  not not_2 (not_2_out, B);
  and and_1 (GT, A, not_2_out);
  and and_2 (LT, not_1_out, B);
  or or_1 (or_1_out, A, B);
  not not_3 (EQ, or_1_out);
endmodule

module MSS (
  input  A,
  input  B,
  output GT,
  output EQ,
  output LT
);

  wire mach_so_sanh_1_eq, mach_so_sanh_1_gt, mach_so_sanh_1_lt, mach_so_sanh_2_lt, mux_2_to_1_1bit_1_y,
       mux_2_to_1_1bit_3_y;

  MACH_SO_SANH mach_so_sanh_1 (.A(A), .B(B), .GT(mach_so_sanh_1_gt), .EQ(mach_so_sanh_1_eq), .LT(mach_so_sanh_1_lt));
  MACH_SO_SANH mach_so_sanh_2 (.A(A), .B(B), .LT(mach_so_sanh_2_lt));  // open: GT, EQ
  MUX_2_TO_1_1BIT mux_2_to_1_1bit_1 (.A(1'b1), .B(mach_so_sanh_1_eq), .Y(mux_2_to_1_1bit_1_y));  // open: S
  MUX_2_TO_1_1BIT mux_2_to_1_1bit_2 (.A(1'b1), .B(mach_so_sanh_1_eq), .Y(EQ));  // open: S
  MUX_2_TO_1_1BIT mux_2_to_1_1bit_3 (.A(1'b1), .B(mach_so_sanh_1_eq), .S(mach_so_sanh_2_lt), .Y(mux_2_to_1_1bit_3_y));
  MUX_2_TO_1_1BIT mux_2_to_1_1bit_4 (.A(mux_2_to_1_1bit_1_y), .B(1'b0), .S(mach_so_sanh_1_gt), .Y(GT));
  MUX_2_TO_1_1BIT mux_2_to_1_1bit_5 (.A(mux_2_to_1_1bit_3_y), .B(1'b0), .S(mach_so_sanh_1_lt), .Y(LT));
endmodule

module Mach_MAx (
  input  A,
  input  B,
  output Max
);

  wire mss_1_eq, mss_1_lt, mux_2_to_1_1bit_2_y;

  MSS mss_1 (.A(A), .B(B), .EQ(mss_1_eq), .LT(mss_1_lt));  // open: GT
  MUX_2_TO_1_1BIT mux_2_to_1_1bit_1 (.A(mux_2_to_1_1bit_2_y), .B(B), .S(mss_1_eq), .Y(Max));
  MUX_2_TO_1_1BIT mux_2_to_1_1bit_2 (.A(A), .B(B), .S(mss_1_lt), .Y(mux_2_to_1_1bit_2_y));
endmodule

module MAX_DONGGOI (
  input  A,
  input  B,
  output Max
);

  Mach_MAx mach_max_1 (.A(A), .B(B), .Max(Max));
endmodule

module MAX_3_SO_2Bit (
  input  A,
  input  B,
  input  C,
  output MAXX
);

  wire mach_max_1_max, mach_so_sanh_1_eq, mach_so_sanh_1_lt, mux_2_to_1_1bit_2_y;

  Mach_MAx mach_max_1 (.A(A), .B(B), .Max(mach_max_1_max));
  MACH_SO_SANH mach_so_sanh_1 (.A(mach_max_1_max), .B(C), .EQ(mach_so_sanh_1_eq), .LT(mach_so_sanh_1_lt));  // open: GT
  MUX_2_TO_1_1BIT mux_2_to_1_1bit_1 (.A(mux_2_to_1_1bit_2_y), .B(C), .S(mach_so_sanh_1_eq), .Y(MAXX));
  MUX_2_TO_1_1BIT mux_2_to_1_1bit_2 (.A(mach_max_1_max), .B(C), .S(mach_so_sanh_1_lt), .Y(mux_2_to_1_1bit_2_y));
endmodule
