// Logisim project LAB4.circ as structural Verilog: 9 circuits, main circuit MUX2_1BIT
module MUX2_1BIT (
  input  A0,
  input  A1,
  input  B0,
  input  B1,
  input  S0,
  input  S1,
  output F
);

  wire multiplexer_1_out, multiplexer_2_out;

  Multiplexer multiplexer_1 (.in0(A0), .in1(A1), .out(multiplexer_1_out), .sel(S0));
  Multiplexer multiplexer_2 (.in0(B0), .in1(B1), .out(multiplexer_2_out), .sel(S0));
  Multiplexer multiplexer_3 (.in0(multiplexer_1_out), .in1(multiplexer_2_out), .out(F), .sel(S1));
endmodule

module MUX4_4BITS (
  input  D0,
  input  D1,
  input  D2,
  input  D3,
  input  DD0,
  input  DD1,
  input  DD2,
  input  DD3,
  input  DDD0,
  input  DDD1,
  input  DDD2,
  input  DDD3,
  input  DDDD0,
  input  DDDD1,
  input  DDDD2,
  input  DDDD3,
  input  S0,
  input  S1,
  output F0,
  output F1,
  output F2,
  output F3
);

  MUX2_1BIT mux2_1bit_1 (.A0(D0), .A1(D1), .B0(D2), .B1(D3), .S0(S0), .S1(S1), .F(F0));
  MUX2_1BIT mux2_1bit_2 (.A0(DD0), .A1(DD1), .B0(DD2), .B1(DD3), .S0(S0), .S1(S1), .F(F1));
  MUX2_1BIT mux2_1bit_3 (.A0(DDD0), .A1(DDD1), .B0(DDD2), .B1(DDD3), .S0(S0), .S1(S1), .F(F2));
  MUX2_1BIT mux2_1bit_4 (.A0(DDDD0), .A1(DDDD1), .B0(DDDD2), .B1(DDDD3), .S0(S0), .S1(S1), .F(F3));
endmodule

module MUX4_4BITS_DONGGOI (
  input  D0,
  input  D1,
  input  D2,
  input  D3,
  input  DD0,
  input  DD1,
  input  DD2,
  input  DD3,
  input  DDD0,
  input  DDD1,
  input  DDD2,
  input  DDD3,
  input  DDDD0,
  input  DDDD1,
  input  DDDD2,
  input  DDDD3,
  input  S0,
  input  S1,
  output F0,
  output F1,
  output F2,
  output F3
);

  MUX4_4BITS mux4_4bits_1 (
    .D0(D0), .D1(D1), .D2(D2), .D3(D3), .DD0(DD0), .DD1(DD1), .DD2(DD2), .DD3(DD3), .DDD0(DDD0), .DDD1(DDD1),
    .DDD2(DDD2), .DDD3(DDD3), .DDDD0(DDDD0), .DDDD1(DDDD1), .DDDD2(DDDD2), .DDDD3(DDDD3), .S0(S0), .S1(S1),
    .F0(F0), .F1(F1), .F2(F2), .F3(F3));
endmodule

module MACH_SO_SANH (
  input  G,
  input  A,
  input  B,
  output GT,
  output EQ,
  output LT
);

  wire not_1_out, not_2_out, not_3_out, or_1_out;

  not not_1 (not_1_out, A);
  not not_2 (not_2_out, B);
  and and_1 (GT, A, not_2_out, G);
  and and_2 (LT, not_1_out, B, G);
  or or_1 (or_1_out, GT, LT);
  not not_3 (not_3_out, or_1_out);
  and and_3 (EQ, not_3_out, G);
endmodule

module MACH_CONG (
  input  I1,
  input  I2,
  input  I3,
  input  I4,
  output A,
  output B,
  output C,
  output D,
  output E,
  output F,
  output G,
  output A1,
  output B1,
  output C1,
  output D1,
  output E1,
  output F1,
  output G1
);


  assign A = 1'b1;
  assign A1 = 1'b0;
  assign B = 1'b1;
  assign B1 = 1'b1;
  assign C = 1'b1;
  assign C1 = 1'b1;
  assign D = 1'b1;
  assign D1 = 1'b0;
  assign E = 1'b1;
  assign E1 = 1'b0;
  assign F = 1'b1;
  assign F1 = 1'b0;
  assign G = 1'b0;
  assign G1 = 1'b0;
endmodule

module MACH_SS_4BITS (
  input  A0,
  input  B0,
  input  A1,
  input  B1,
  input  A2,
  input  B2,
  input  A3,
  input  B3,
  output GT,
  output LT,
  output EQ
);

  wire mach_so_sanh_1_eq, mach_so_sanh_1_gt, mach_so_sanh_1_lt, mach_so_sanh_2_eq, mach_so_sanh_2_gt,
       mach_so_sanh_2_lt, mach_so_sanh_3_eq, mach_so_sanh_3_gt, mach_so_sanh_3_lt, mach_so_sanh_4_gt,
       mach_so_sanh_4_lt;

  MACH_SO_SANH mach_so_sanh_1 (
    .G(1'b1), .A(A0), .B(B0), .GT(mach_so_sanh_1_gt), .EQ(mach_so_sanh_1_eq), .LT(mach_so_sanh_1_lt));
  MACH_SO_SANH mach_so_sanh_2 (
    .G(mach_so_sanh_1_eq), .A(A1), .B(B1), .GT(mach_so_sanh_2_gt), .EQ(mach_so_sanh_2_eq),
    .LT(mach_so_sanh_2_lt));
  MACH_SO_SANH mach_so_sanh_3 (
    .G(mach_so_sanh_2_eq), .A(A2), .B(B2), .GT(mach_so_sanh_3_gt), .EQ(mach_so_sanh_3_eq),
    .LT(mach_so_sanh_3_lt));
  MACH_SO_SANH mach_so_sanh_4 (
    .G(mach_so_sanh_3_eq), .A(A3), .B(B3), .GT(mach_so_sanh_4_gt), .EQ(EQ), .LT(mach_so_sanh_4_lt));
  or or_1 (GT, mach_so_sanh_1_gt, mach_so_sanh_2_gt, mach_so_sanh_4_gt, mach_so_sanh_3_gt);
  or or_2 (LT, mach_so_sanh_1_lt, mach_so_sanh_2_lt, mach_so_sanh_4_lt, mach_so_sanh_3_lt);
endmodule

module EG_4Bits (
  input  a0,
  input  b0,
  input  a1,
  input  b1,
  input  a2,
  input  b2,
  input  a3,
  input  b3,
  output EQ
);

  wire xnor_1_out, xnor_2_out, xnor_3_out, xnor_4_out;

  xnor xnor_1 (xnor_1_out, a0, b0);
  xnor xnor_2 (xnor_2_out, a1, b1);
  xnor xnor_3 (xnor_3_out, a2, b2);
  xnor xnor_4 (xnor_4_out, a3, b3);
  and and_1 (EQ, xnor_1_out, xnor_2_out, xnor_3_out, xnor_4_out);
endmodule

module LT_4Bits (
  input  a0,
  input  b0,
  input  a1,
  input  b1,
  input  a2,
  input  b2,
  input  a3,
  input  b3,
  output LT
);

  wire and_1_out, and_2_out, and_3_out, and_4_out, not_1_out, not_2_out, not_3_out, not_4_out, xnor_1_out,
       xnor_2_out, xnor_3_out;

  xnor xnor_1 (xnor_1_out, a1, b1);
  xnor xnor_2 (xnor_2_out, a2, xnor_3_out);
  xnor xnor_3 (xnor_3_out, a3, b3);
  not not_1 (not_1_out, a0);
  not not_2 (not_2_out, a1);
  not not_3 (not_3_out, a2);
  not not_4 (not_4_out, a3);
  and and_1 (and_1_out, not_1_out, b0, xnor_2_out, xnor_3_out, xnor_1_out);
  and and_2 (and_2_out, not_2_out, b1, xnor_3_out, xnor_2_out);
  and and_3 (and_3_out, not_3_out, b2, xnor_3_out);
  and and_4 (and_4_out, not_4_out, b3);
  or or_1 (LT, and_1_out, and_2_out, and_3_out, and_4_out);
endmodule

module GT_4Bits (
  input  a0,
  input  b0,
  input  a1,
  input  b1,
  input  a2,
  input  b2,
  input  a3,
  input  b3,
  output GT
);

  wire and_1_out, and_2_out, and_3_out, and_4_out, not_1_out, not_2_out, not_3_out, not_4_out, xnor_1_out,
       xnor_2_out, xnor_3_out;

  not not_1 (not_1_out, b0);
  xnor xnor_1 (xnor_1_out, a1, xnor_2_out);
  not not_2 (not_2_out, b1);
  xnor xnor_2 (xnor_2_out, a2, xnor_3_out);
  not not_3 (not_3_out, b2);
  xnor xnor_3 (xnor_3_out, a3, not_4_out);
  not not_4 (not_4_out, b3);
  and and_1 (and_1_out, a0, not_1_out, xnor_2_out, xnor_3_out, xnor_1_out);
  and and_2 (and_2_out, a1, not_2_out, xnor_3_out, xnor_2_out);
  and and_3 (and_3_out, a2, not_3_out, xnor_3_out);
  and and_4 (and_4_out, a3, not_4_out);
  or or_1 (GT, and_1_out, and_2_out, and_3_out, and_4_out);
endmodule
