// Logisim project LAB4_EX.circ as structural Verilog: 2 circuits, main circuit main
module main (
  input  [3:0] A,
  input  [3:0] B,
  output [3:0] out_3,
  output [3:0] out_4
);

  wire comparator_1_lt;

  Comparator #(.width(4)) comparator_1 (.a(A), .b(B), .lt(comparator_1_lt));  // open: gt, eq
  Multiplexer #(.width(4)) multiplexer_1 (.in0(A), .in1(B), .out(out_3), .sel(comparator_1_lt));
endmodule

module main2 (
  input  [3:0] A,
  input  [3:0] B,
  input  [3:0] C,
  output [3:0] out_4
);

  wire comparator_1_lt, comparator_2_lt, comparator_3_lt;
  wire [3:0] multiplexer_1_out, multiplexer_2_out;

  Comparator #(.width(4)) comparator_1 (.a(A), .b(B), .lt(comparator_1_lt));  // open: gt, eq
  Multiplexer #(.width(4)) multiplexer_1 (.in0(A), .in1(B), .out(multiplexer_1_out), .sel(comparator_1_lt));
  Comparator #(.width(4)) comparator_2 (.a(B), .b(C), .lt(comparator_2_lt));  // open: gt, eq
  Multiplexer #(.width(4)) multiplexer_2 (.in0(B), .in1(C), .out(multiplexer_2_out), .sel(comparator_2_lt));
  Comparator #(.width(4)) comparator_3 (
    .a(multiplexer_1_out), .b(multiplexer_2_out), .lt(comparator_3_lt));  // open: gt, eq
  Multiplexer #(.width(4)) multiplexer_3 (
    .in0(multiplexer_1_out), .in1(multiplexer_2_out), .out(out_4), .sel(comparator_3_lt));
endmodule
